// Digital circuit RF_ALU_Top.dig as structural Verilog
module RF_ALU_Top (
  input  CLK,
  input  WE,
  input  WriteReg0,
  input  WriteReg1,
  input  ReadRed1_0,
  input  ReadRed1_1,
  input  ReadRed2_0,
  input  ReadRed2_1,
  input  S0,
  input  S1,
  input  Cin
);

  wire alu4_1_p12, alu4_1_p13, alu4_1_p14, alu4_1_p15, registerfile_1_readdata1_0,
       registerfile_1_readdata1_1, registerfile_1_readdata1_2, registerfile_1_readdata1_3,
       registerfile_1_readdata2_0, registerfile_1_readdata2_1, registerfile_1_readdata2_2,
       registerfile_1_readdata2_3;

  RegisterFile registerfile_1 (
    .D3(alu4_1_p15), .D2(alu4_1_p14), .D1(alu4_1_p13), .D0(alu4_1_p12), .WE(WE), .CLK(CLK),
    .WriteReg0(WriteReg0), .WriteReg1(WriteReg1), .ReadReg1_0(ReadRed1_0), .ReadReg1_1(ReadRed1_1),
    .ReadReg2_0(ReadRed2_0), .ReadReg2_1(ReadRed2_1), .ReadData1_3(registerfile_1_readdata1_3),
    .ReadData1_2(registerfile_1_readdata1_2), .ReadData1_1(registerfile_1_readdata1_1),
    .ReadData1_0(registerfile_1_readdata1_0), .ReadData2_3(registerfile_1_readdata2_3),
    .ReadData2_2(registerfile_1_readdata2_2), .ReadData2_1(registerfile_1_readdata2_1),
    .ReadData2_0(registerfile_1_readdata2_0));
  // ALU4 alu4_1: pin names not known; wires that end beside it: registerfile_1_readdata1_0, registerfile_1_readdata2_0, S0, S1, Cin, registerfile_1_readdata1_1, registerfile_1_readdata2_1, registerfile_1_readdata1_2, registerfile_1_readdata2_2, registerfile_1_readdata1_3, registerfile_1_readdata2_3, alu4_1_p12, alu4_1_p13, alu4_1_p14, alu4_1_p15
endmodule
