// Digital circuit Reg4.dig as structural Verilog
module Reg4 (
  input  D3,
  input  D2,
  input  D1,
  input  D0,
  input  CLK,
  input  EN,
  output Q3,
  output Q2,
  output Q1,
  output Q0
);

  wire and_1_out;

  and and_1 (and_1_out, CLK, EN);
  D_FF d_ff_1 (.D(D3), .C(and_1_out), .nQ(Q3));  // open: Q
  D_FF d_ff_2 (.D(D2), .C(and_1_out), .nQ(Q2));  // open: Q
  D_FF d_ff_3 (.D(D1), .C(and_1_out), .nQ(Q1));  // open: Q
  D_FF d_ff_4 (.D(D0), .C(and_1_out), .nQ(Q0));  // open: Q
endmodule
