// Digital circuit RegisterFile.dig as structural Verilog
module RegisterFile (
  input  D3,
  input  D2,
  input  D1,
  input  D0,
  input  WE,
  input  CLK,
  input  WriteReg0,
  input  WriteReg1,
  input  ReadReg1_0,
  input  ReadReg1_1,
  input  ReadReg2_0,
  input  ReadReg2_1,
  output ReadData1_3,
  output ReadData1_2,
  output ReadData1_1,
  output ReadData1_0,
  output ReadData2_3,
  output ReadData2_2,
  output ReadData2_1,
  output ReadData2_0
);

  wire and_1_out, and_2_out, and_3_out, and_4_out, multiplexer_1_out, multiplexer_2_out, multiplexer_3_out,
       multiplexer_4_out, multiplexer_5_out, multiplexer_6_out, multiplexer_7_out, multiplexer_8_out,
       multiplexer_9_out, multiplexer_10_out, multiplexer_11_out, multiplexer_12_out, multiplexer_13_out,
       multiplexer_14_out, multiplexer_15_out, multiplexer_16_out, not_1_out, not_2_out, R0_q0, R0_q1, R0_q2,
       R0_q3, R1_q0, R1_q1, R1_q2, R1_q3, R2_q0, R2_q1, R2_q2, R2_q3, R3_q1, R3_q2, R3_q3;

  not not_1 (not_1_out, WriteReg1);
  not not_2 (not_2_out, WriteReg0);
  and and_1 (and_1_out, WE, not_1_out, not_2_out);
  and and_2 (and_2_out, WE, not_1_out, WriteReg0);
  and and_3 (and_3_out, WE, WriteReg1, not_2_out);
  and and_4 (and_4_out, WE, WriteReg1, WriteReg0);
  Reg4 R0 (
    .D3(D3), .D2(D2), .D1(D1), .D0(D0), .CLK(CLK), .EN(and_1_out), .Q3(R0_q3), .Q2(R0_q2), .Q1(R0_q1),
    .Q0(R0_q0));
  Reg4 R1 (
    .D3(D3), .D2(D2), .D1(D1), .D0(D0), .CLK(CLK), .EN(and_2_out), .Q3(R1_q3), .Q2(R1_q2), .Q1(R1_q1),
    .Q0(R1_q0));
  Reg4 R2 (
    .D3(D3), .D2(D2), .D1(D1), .D0(D0), .CLK(CLK), .EN(and_3_out), .Q3(R2_q3), .Q2(R2_q2), .Q1(R2_q1),
    .Q0(R2_q0));
  Reg4 R3 (
    .D3(D3), .D2(D2), .D1(D1), .D0(D0), .CLK(CLK), .EN(and_4_out), .Q3(R3_q3), .Q2(R3_q2), .Q1(R3_q1),
    .Q0(R3_q3));
  Multiplexer multiplexer_1 (.sel(ReadReg1_0), .in_0(R0_q0), .in_1(R1_q0), .out(multiplexer_1_out));
  Multiplexer multiplexer_2 (.sel(ReadReg1_0), .in_0(R2_q0), .in_1(R3_q3), .out(multiplexer_2_out));
  Multiplexer multiplexer_3 (.sel(ReadReg1_0), .in_0(R0_q1), .in_1(R1_q1), .out(multiplexer_3_out));
  Multiplexer multiplexer_4 (.sel(ReadReg1_0), .in_0(R2_q1), .in_1(R3_q1), .out(multiplexer_4_out));
  Multiplexer multiplexer_5 (.sel(ReadReg1_0), .in_0(R0_q2), .in_1(R1_q2), .out(multiplexer_5_out));
  Multiplexer multiplexer_6 (.sel(ReadReg1_0), .in_0(R2_q2), .in_1(R3_q2), .out(multiplexer_6_out));
  Multiplexer multiplexer_7 (.sel(ReadReg1_0), .in_0(R0_q3), .in_1(R1_q3), .out(multiplexer_7_out));
  Multiplexer multiplexer_8 (.sel(ReadReg1_0), .in_0(R2_q3), .in_1(R3_q3), .out(multiplexer_8_out));
  Multiplexer multiplexer_9 (.sel(ReadReg2_0), .in_0(R0_q0), .in_1(R1_q0), .out(multiplexer_9_out));
  Multiplexer multiplexer_10 (.sel(ReadReg2_0), .in_0(R2_q0), .in_1(R3_q3), .out(multiplexer_10_out));
  Multiplexer multiplexer_11 (.sel(ReadReg2_0), .in_0(R0_q1), .in_1(R1_q1), .out(multiplexer_11_out));
  Multiplexer multiplexer_12 (.sel(ReadReg2_0), .in_0(R2_q1), .in_1(R3_q1), .out(multiplexer_12_out));
  Multiplexer multiplexer_13 (.sel(ReadReg2_0), .in_0(R0_q2), .in_1(R1_q2), .out(multiplexer_13_out));
  Multiplexer multiplexer_14 (.sel(ReadReg2_0), .in_0(R2_q2), .in_1(R3_q2), .out(multiplexer_14_out));
  Multiplexer multiplexer_15 (.sel(ReadReg2_0), .in_0(R0_q3), .in_1(R1_q3), .out(multiplexer_15_out));
  Multiplexer multiplexer_16 (.sel(ReadReg2_0), .in_0(R2_q3), .in_1(R3_q3), .out(multiplexer_16_out));
  Multiplexer multiplexer_17 (.sel(ReadReg1_1), .in_0(multiplexer_1_out), .in_1(multiplexer_2_out), .out(ReadData1_0));
  Multiplexer multiplexer_18 (.sel(ReadReg1_1), .in_0(multiplexer_3_out), .in_1(multiplexer_4_out), .out(ReadData1_1));
  Multiplexer multiplexer_19 (.sel(ReadReg1_1), .in_0(multiplexer_5_out), .in_1(multiplexer_6_out), .out(ReadData1_2));
  Multiplexer multiplexer_20 (.sel(ReadReg1_1), .in_0(multiplexer_7_out), .in_1(multiplexer_8_out), .out(ReadData1_3));
  Multiplexer multiplexer_21 (.sel(ReadReg2_1), .in_0(multiplexer_9_out), .in_1(multiplexer_10_out), .out(ReadData2_0));
  Multiplexer multiplexer_22 (
    .sel(ReadReg2_1), .in_0(multiplexer_11_out), .in_1(multiplexer_12_out), .out(ReadData2_1));
  Multiplexer multiplexer_23 (
    .sel(ReadReg2_1), .in_0(multiplexer_13_out), .in_1(multiplexer_14_out), .out(ReadData2_2));
  Multiplexer multiplexer_24 (
    .sel(ReadReg2_1), .in_0(multiplexer_15_out), .in_1(multiplexer_16_out), .out(ReadData2_3));
endmodule
